// Logisim project CPU.circ as structural Verilog
module ALU (
  input  [3:0] A,
  input  [3:0] B,
  input  [3:0] OP,
  input  [1:0] K,
  input  CF,
  output [3:0] Y,
  output [3:0] HIN,
  output Z,
  output C,
  output N,
  output V,
  output DIVZ
);

  wire and_1_out, and_2_out, CADD, CIN, D1, D2, D3, D4, D14, HNZ, SC, SUBM, VADD, xnor_1_out, xor_3_out;
  wire [3:0] AN, BDIV, BP, MASK, NT, ORR, PH, PL, Q, REM_t, ROLY, RORY, S, SHLH, SHLL, SHRH, SHRY, SUBM4, XR;

  or or_1 (SUBM, D2, D3, D14);
  nor nor_1 (DIVZ, BP[0], BP[1], BP[2], BP[3]);
  Multiplexer #(.select(4), .width(4)) multiplexer_1 (
    .in0(S), .in1(S), .in2(S), .in3(S), .in4(PL), .in5(Q), .in6(AN), .in7(ORR), .in8(XR), .in9(NT),
    .in10(SHLL), .in11(SHRY), .in12(ROLY), .in13(RORY), .in14(S), .in15(S), .out(Y), .sel(OP));
  assign SUBM4 = {{3{SUBM}}, SUBM};  // Bit_Extender bit_extender_1
  Decoder #(.enable("false"), .select(4)) decoder_1 (
    .out1(D1), .out2(D2), .out3(D3), .out4(D4), .out14(D14), .sel(OP));  // open: out0, out5, out6, out7, out8, out9, out10, out11, out12, out13, out15
  assign BP = B ^ SUBM4;  // XOR_Gate xor_1, 4 bits wide
  // Probe on DIVZ
  // Probe on Y
  // Probe on BDIV
  Multiplexer #(.width(4)) multiplexer_2 (.in0(B), .in1(4'b0001), .out(BDIV), .sel(DIVZ));
  // Probe on Q
  Divider #(.width(4)) divider_1 (.a(A), .b(BDIV), .out(Q), .upper(4'b0000), .rem(REM_t));
  // Probe on REM_t
  // Probe on PL
  Multiplier #(.width(4)) multiplier_1 (.a(A), .b(B), .out(PL), .cin(4'b0000), .cout(PH));
  // Probe on PH
  Multiplexer #(.select(4), .width(4)) multiplexer_3 (
    .in0(4'b0000), .in1(4'b0000), .in2(4'b0000), .in3(4'b0000), .in4(PH), .in5(REM_t), .in6(4'b0000),
    .in7(4'b0000), .in8(4'b0000), .in9(4'b0000), .in10(SHLH), .in11(SHRH), .in12(4'b0000), .in13(4'b0000),
    .in14(4'b0000), .in15(4'b0000), .out(HIN), .sel(OP));
  // Probe on HIN
  and and_1 (and_1_out, D1, CF);
  and and_2 (and_2_out, D3, ~CF);  // AND_Gate
  // Probe on SC
  xor xor_2 (CADD, SUBM, SC);
  Adder #(.width(4)) adder_1 (.a(A), .b(BP), .out(S), .cin(CIN), .cout(SC));
  // Probe on CADD
  Multiplexer #(.select(2), .width(4)) multiplexer_4 (
    .in0(4'b0000), .in1(4'b0001), .in2(4'b0011), .in3(4'b0111), .out(MASK), .sel(K));
  or or_2 (CIN, and_1_out, and_2_out, D2, D14);
  // Probe on S
  xnor xnor_1 (xnor_1_out, A[3], BP[3]);
  xor xor_3 (xor_3_out, A[3], S[3]);
  or or_3 (HNZ, HIN[0], HIN[1], HIN[2], HIN[3]);
  and and_3 (VADD, xnor_1_out, xor_3_out);
  // Probe on VADD
  assign SHRH = A & MASK;  // AND_Gate and_4, 4 bits wide
  // Probe on SHRH
  assign AN = A & B;  // AND_Gate and_5, 4 bits wide
  assign ORR = A | B;  // OR_Gate or_4, 4 bits wide
  assign XR = A ^ B;  // XOR_Gate xor_4, 4 bits wide
  assign NT = ~A;  // NOT_Gate not_1, 4 bits wide
  Shifter shifter_1 (.in({4'b0000, A}), .\dist ({1'b0, K}), .out({SHLH, SHLL}));
  Shifter #(.shift("lr"), .width(4)) shifter_2 (.in(A), .\dist (K), .out(SHRY));
  // Probe on SHRY
  // Probe on SHLL
  // Probe on SHLH
  // Probe on ROLY
  Shifter #(.shift("rl"), .width(4)) shifter_3 (.in(A), .\dist (K), .out(ROLY));
  Shifter #(.shift("rr"), .width(4)) shifter_4 (.in(A), .\dist (K), .out(RORY));
  // Probe on RORY
endmodule
