// Logisim project Lock.circ as structural Verilog
module EDGE_DETECT (
  input  BTN,
  input  CLK,
  output EV,
  output PREV
);

  wire not_1_out;

  D_Flip_Flop d_ff_1 (.D(BTN), .clk(CLK), .Q(PREV));  // open: Qn, preset, reset
  not not_1 (not_1_out, PREV);
  and and_1 (EV, BTN, not_1_out);

  // Notes on the sheet:
  //   PREV: Previous button value
  //   EV: Detect if a button is activated which was previously not
endmodule

module EVENT_LOGIC (
  input  RUN,
  input  RESET,
  input  S1,
  input  S0,
  input  CLR_EV,
  input  ENT_EV,
  input  [3:0] DIGIT,
  output EN,
  output IN_ENTRY,
  output IN_UNL,
  output DO_CLEAR,
  output VALID_ENT,
  output INV_ENT
);

  wire DO_ENTER, INV, or_1_out;

  and and_1 (EN, RUN, ~RESET);  // AND_Gate
  or or_1 (or_1_out, DIGIT[1], DIGIT[2]);
  nor nor_1 (IN_ENTRY, S1, S0);
  and and_2 (IN_UNL, ~S1, S0);  // AND_Gate
  and and_3 (INV, or_1_out, DIGIT[3]);
  and and_4 (DO_CLEAR, EN, IN_ENTRY, CLR_EV);
  and and_5 (DO_ENTER, EN, ~CLR_EV, ENT_EV, IN_ENTRY);  // AND_Gate
  and and_6 (VALID_ENT, DO_ENTER, ~INV);  // AND_Gate
  and and_7 (INV_ENT, DO_ENTER, INV);

  // Notes on the sheet:
  //   S : 00 :  IN ENTRY
  //   01 : UNCLOCKED
  //   10 : LOCKED
  //   CLR_EV : Clear Event
  //   ENT_EV : Enter Event
  //   EN : Running and not Reset
  //   DO_CLEAR : Clear event and in entry
  //   INV : Invalid digits (10-15)
  //   VALID_ENT : Valid entry
  //   INV_ENT : Invalid Entry
  //   DO_ENTER : Enter event and in entry
endmodule

module RESULT_LOGIC (
  input  [1:0] CNT,
  input  VALID_ENT,
  input  MATCH,
  input  [1:0] ATT,
  output C_IS0,
  output C_IS3,
  output LD1,
  output LD2,
  output LD3,
  output COMPLETE,
  output CORRECT,
  output WRONG,
  output LOCK3
);

  wire C_IS1, C_IS2;

  Decoder #(.select(2)) decoder_1 (.out0(C_IS0), .out1(C_IS1), .out2(C_IS2), .out3(C_IS3), .sel(CNT));  // open: en
  and and_1 (LD1, C_IS0, VALID_ENT);
  and and_2 (LD2, C_IS1, VALID_ENT);
  and and_3 (LD3, C_IS2, VALID_ENT);
  and and_4 (COMPLETE, VALID_ENT, C_IS3);
  and and_5 (CORRECT, MATCH, COMPLETE);
  and and_6 (WRONG, COMPLETE, ~MATCH);  // AND_Gate
  and and_7 (LOCK3, WRONG, ~ATT[0], ATT[1]);  // AND_Gate

  // Notes on the sheet:
  //   CNT : No. of digits entered
  //   ATT :  No. of attempts
  //   VALID_ENT : from EVENT_LOGIC
  //   MATCH : from PIN_COMPARE
  //   C_IS[0:3] : Counter Position Indicators
  //   LD[1:3] : Load ith character
  //   CORRECT : Complete and Match
  //   WRONG : Complete and not Match
  //   LOCK3 : Lock out after 3rd failure
  //   COMPLETE : Indicates final digit has been entered
endmodule

module PIN_COMPARE (
  input  [3:0] R1,
  input  [3:0] R2,
  input  [3:0] R3,
  input  [3:0] DIGIT,
  output MATCH
);

  wire comparator_1_eq, comparator_2_eq, comparator_3_eq, comparator_4_eq;

  Comparator #(.width(4)) comparator_1 (.a(4'b0010), .b(R1), .eq(comparator_1_eq));  // open: gt, lt
  Comparator #(.width(4)) comparator_2 (.a(4'b0100), .b(R2), .eq(comparator_2_eq));  // open: gt, lt
  Comparator #(.width(4)) comparator_3 (.a(4'b0110), .b(R3), .eq(comparator_3_eq));  // open: gt, lt
  Comparator #(.width(4)) comparator_4 (.a(4'b1000), .b(DIGIT), .eq(comparator_4_eq));  // open: gt, lt
  and and_1 (MATCH, comparator_1_eq, comparator_2_eq, comparator_3_eq, comparator_4_eq);
endmodule

module DIGIT_STORE (
  input  CLR_STORE,
  input  [3:0] DIGIT,
  input  LD1,
  input  LD2,
  input  CLK,
  input  LD3,
  output [3:0] R1,
  output [3:0] R2,
  output [3:0] R3
);

  wire or_1_out, or_2_out, or_3_out;
  wire [3:0] multiplexer_1_out;

  Multiplexer #(.width(4)) multiplexer_1 (.in0(DIGIT), .in1(4'b0000), .out(multiplexer_1_out), .sel(CLR_STORE));
  or or_1 (or_1_out, CLR_STORE, LD1);
  or or_2 (or_2_out, CLR_STORE, LD2);
  or or_3 (or_3_out, CLR_STORE, LD3);
  Register #(.width(4)) register_1 (.D(multiplexer_1_out), .en(or_1_out), .clk(CLK), .Q(R1), .clr(1'b0));
  Register #(.width(4)) register_2 (.D(multiplexer_1_out), .en(or_2_out), .clk(CLK), .Q(R2), .clr(1'b0));
  Register #(.width(4)) register_3 (.D(multiplexer_1_out), .en(or_3_out), .clk(CLK), .Q(R3), .clr(1'b0));
endmodule
